// Logisim project 8-bit Register file.circ as structural Verilog
module _8__bit_register_file (
  input  [2:0] Write_Register,
  input  [2:0] Read_Register_2,
  input  [7:0] Input,
  input  [2:0] Read_Register_2_2,
  input  Write_Control,
  output [7:0] Read_Data_1,
  output [7:0] Read_Data_2
);

  wire and_1_out, and_2_out, and_3_out, and_4_out, and_5_out, and_6_out, decoder_1_out0, decoder_1_out1,
       decoder_1_out2, decoder_1_out3, decoder_1_out4, decoder_1_out5;
  wire [7:0] register_1_q, register_2_q, register_3_q, register_4_q, register_5_q, register_6_q;

  Decoder #(.select(3)) decoder_1 (
    .out0(decoder_1_out0), .out1(decoder_1_out1), .out2(decoder_1_out2), .out3(decoder_1_out3),
    .out4(decoder_1_out4), .out5(decoder_1_out5), .sel(Write_Register));  // open: out6, out7, en
  and and_1 (and_1_out, decoder_1_out0, Write_Control);
  and and_2 (and_2_out, decoder_1_out1, Write_Control);
  and and_3 (and_3_out, decoder_1_out2, Write_Control);
  and and_4 (and_4_out, decoder_1_out3, Write_Control);
  and and_5 (and_5_out, decoder_1_out4, Write_Control);
  and and_6 (and_6_out, decoder_1_out5, Write_Control);
  Register register_1 (.D(Input), .en(and_1_out), .Q(register_1_q));  // open: clk, clr
  Register register_2 (.D(Input), .en(and_2_out), .Q(register_2_q));  // open: clk, clr
  Register register_3 (.D(Input), .en(and_3_out), .Q(register_3_q));  // open: clk, clr
  Register register_4 (.D(Input), .en(and_4_out), .Q(register_4_q));  // open: clk, clr
  Register register_5 (.D(Input), .en(and_5_out), .Q(register_5_q));  // open: clk, clr
  Register register_6 (.D(Input), .en(and_6_out), .Q(register_6_q));  // open: clk, clr
  Multiplexer #(.select(3), .width(8)) multiplexer_1 (
    .in0(register_1_q), .in1(register_2_q), .in2(register_3_q), .in3(register_4_q), .in4(register_5_q),
    .in5(register_6_q), .out(Read_Data_1), .sel(Read_Register_2));  // open: in6, in7, en
  Multiplexer #(.select(3), .width(8)) multiplexer_2 (
    .in0(register_1_q), .in1(register_2_q), .in2(register_3_q), .in3(register_4_q), .in4(register_5_q),
    .in5(register_6_q), .out(Read_Data_2), .sel(Read_Register_2_2));  // open: in6, in7, en
endmodule

module _1_bit_ALU (
  input  Cin,
  input  A,
  input  B,
  input  [2:0] Operation_Selection,
  output out_5,
  output Cout
);

  wire adder_1_out, and_1_out, not_1_out, not_2_out, xor_1_out;

  not not_1 (not_1_out, B);
  not not_2 (not_2_out, A);
  and and_1 (and_1_out, A, B);
  xor xor_1 (xor_1_out, A, B);
  Adder #(.width(1)) adder_1 (.a(A), .b(B), .out(adder_1_out), .cin(Cin), .cout(Cout));
  Multiplexer #(.select(3)) multiplexer_1 (
    .in2(and_1_out), .in3(xor_1_out), .in4(adder_1_out), .in5(not_2_out), .in6(not_1_out), .out(out_5),
    .sel(Operation_Selection));  // open: in0, in1, in7, en
endmodule

module _8_bit_ALU (
  input  Cin,
  input  [7:0] Input_1,
  input  [7:0] Input_2,
  input  [2:0] Op,
  output [7:0] Output,
  output Cout
);

  wire n1_bit_alu_1_cout, n1_bit_alu_2_cout, n1_bit_alu_3_cout, n1_bit_alu_4_cout, n1_bit_alu_5_cout,
       n1_bit_alu_6_cout, n1_bit_alu_7_cout;

  _1_bit_ALU u_1_bit_alu_1 (
    .Cin(Cin), .A(Input_1[0]), .B(Input_2[0]), .out_5(Output[0]), .Cout(n1_bit_alu_1_cout),
    .Operation_Selection(Op));
  _1_bit_ALU u_1_bit_alu_2 (
    .Cin(n1_bit_alu_1_cout), .A(Input_1[1]), .B(Input_2[1]), .out_5(Output[1]), .Cout(n1_bit_alu_2_cout),
    .Operation_Selection(Op));
  _1_bit_ALU u_1_bit_alu_3 (
    .Cin(n1_bit_alu_2_cout), .A(Input_1[2]), .B(Input_2[2]), .out_5(Output[2]), .Cout(n1_bit_alu_3_cout),
    .Operation_Selection(Op));
  _1_bit_ALU u_1_bit_alu_4 (
    .Cin(n1_bit_alu_3_cout), .A(Input_1[3]), .B(Input_2[3]), .out_5(Output[3]), .Cout(n1_bit_alu_4_cout),
    .Operation_Selection(Op));
  _1_bit_ALU u_1_bit_alu_5 (
    .Cin(n1_bit_alu_4_cout), .A(Input_1[4]), .B(Input_2[4]), .out_5(Output[4]), .Cout(n1_bit_alu_5_cout),
    .Operation_Selection(Op));
  _1_bit_ALU u_1_bit_alu_6 (
    .Cin(n1_bit_alu_5_cout), .A(Input_1[5]), .B(Input_2[5]), .out_5(Output[5]), .Cout(n1_bit_alu_6_cout),
    .Operation_Selection(Op));
  _1_bit_ALU u_1_bit_alu_7 (
    .Cin(n1_bit_alu_6_cout), .A(Input_1[6]), .B(Input_2[6]), .out_5(Output[6]), .Cout(n1_bit_alu_7_cout),
    .Operation_Selection(Op));
  _1_bit_ALU u_1_bit_alu_8 (
    .Cin(n1_bit_alu_7_cout), .A(Input_1[7]), .B(Input_2[7]), .out_5(Output[7]), .Cout(Cout),
    .Operation_Selection(Op));
endmodule
