// Logisim project CSE332_05_LAB_01.circ as structural Verilog: 1 circuit, main circuit main
module main (
  input  A1,
  input  B1,
  input  [1:0] S1___S0,
  input  A0,
  input  B0,
  output F1,
  output F0
);

  wire AND_2_out, AND_out, NOT_2_out, NOT_out, OR_2_out, OR_out, XOR_2_out, XOR_out;

  and AND (AND_out, A1, B1);
  or OR (OR_out, A1, B1);
  xor XOR (XOR_out, A1, B1);
  not NOT (NOT_out, A1);
  and AND_2 (AND_2_out, A0, B0);
  or OR_2 (OR_2_out, A0, B0);
  xor XOR_2 (XOR_2_out, A0, B0);
  not NOT_2 (NOT_2_out, A0);
  Multiplexer #(.select(2)) multiplexer_1 (
    .in0(AND_out), .in1(OR_out), .in2(XOR_out), .in3(NOT_out), .out(F1), .sel(S1___S0));  // open: en
  Multiplexer #(.select(2)) multiplexer_2 (
    .in0(AND_2_out), .in1(OR_2_out), .in2(XOR_2_out), .in3(NOT_2_out), .out(F0), .sel(S1___S0));  // open: en
endmodule
