// Logisim project  lab3_classwork_cse332l.5_fall2020.circ as structural Verilog: 1 circuit, main circuit main
module main (
  input  [1:0] S1__S0,
  input  Right_Shift_Register,
  input  Left_Shift_Register,
  input  I4,
  input  I3,
  input  I2,
  input  I1,
  output A4,
  output A3,
  output A2,
  output A1
);

  wire Clock_out, CLR_out, multiplexer_1_out, multiplexer_2_out, multiplexer_3_out, multiplexer_4_out;

  Button CLR (.out(CLR_out));
  Clock Clock (.out(Clock_out));
  D_Flip_Flop F4 (.clk(Clock_out), .D(multiplexer_1_out), .Q(A4), .reset(CLR_out));  // open: Qn, preset, en
  Multiplexer #(.select(2)) multiplexer_1 (
    .in0(A4), .in1(Right_Shift_Register), .in2(A3), .in3(I4), .out(multiplexer_1_out), .sel(S1__S0));  // open: en
  D_Flip_Flop F3 (.clk(Clock_out), .D(multiplexer_2_out), .Q(A3), .reset(CLR_out));  // open: Qn, preset, en
  Multiplexer #(.select(2)) multiplexer_2 (
    .in0(A3), .in1(A4), .in2(A2), .in3(I3), .out(multiplexer_2_out), .sel(S1__S0));  // open: en
  D_Flip_Flop F2 (.clk(Clock_out), .D(multiplexer_3_out), .Q(A2), .reset(CLR_out));  // open: Qn, preset, en
  Multiplexer #(.select(2)) multiplexer_3 (
    .in0(A2), .in1(A3), .in2(A1), .in3(I2), .out(multiplexer_3_out), .sel(S1__S0));  // open: en
  D_Flip_Flop F1 (.clk(Clock_out), .D(multiplexer_4_out), .Q(A1), .reset(CLR_out));  // open: Qn, preset, en
  Multiplexer #(.select(2)) multiplexer_4 (
    .in0(A1), .in1(A2), .in2(Left_Shift_Register), .in3(I1), .out(multiplexer_4_out), .sel(S1__S0));  // open: en
endmodule
