// Logisim project  lab5_classwork_cse332l.5_fall2020.circ as structural Verilog: 2 circuits, main circuit main
module main (
);

  _4_bit_Register u_4_bit_register_1 ();  // open: Write_Data, Write_Control, Read_Data_1, Write_register, RS, Read_Data_2, RD, CLK
endmodule

module _4_bit_Register (
  input  [2:0] Write_register,
  input  [2:0] RS,
  input  [2:0] RD,
  input  [3:0] Write_Data,
  input  Write_Control,
  input  CLK,
  output [3:0] Read_Data_1,
  output [3:0] Read_Data_2
);

  wire and_1_out, and_2_out, and_3_out, and_4_out, and_5_out, and_6_out, and_7_out, and_8_out,
       decoder_1_out0, decoder_1_out1, decoder_1_out2, decoder_1_out3, decoder_1_out4, decoder_1_out5,
       decoder_1_out6, decoder_1_out7;
  wire [3:0] register_1_q, register_2_q, register_3_q, register_4_q, register_5_q, register_6_q,
       register_7_q, register_8_q;

  Decoder #(.select(3)) decoder_1 (
    .out0(decoder_1_out0), .out1(decoder_1_out1), .out2(decoder_1_out2), .out3(decoder_1_out3),
    .out4(decoder_1_out4), .out5(decoder_1_out5), .out6(decoder_1_out6), .out7(decoder_1_out7),
    .sel(Write_register));  // open: en
  and and_1 (and_1_out, decoder_1_out0, Write_Control);
  and and_2 (and_2_out, decoder_1_out1, Write_Control);
  and and_3 (and_3_out, decoder_1_out2, Write_Control);
  and and_4 (and_4_out, decoder_1_out3, Write_Control);
  and and_5 (and_5_out, decoder_1_out4, Write_Control);
  and and_6 (and_6_out, decoder_1_out5, Write_Control);
  and and_7 (and_7_out, decoder_1_out6, Write_Control);
  and and_8 (and_8_out, decoder_1_out7, Write_Control);
  Register #(.width(4)) register_1 (.D(Write_Data), .en(and_1_out), .Q(register_1_q), .clk(CLK));  // open: clr
  Register #(.width(4)) register_2 (.D(Write_Data), .en(and_2_out), .Q(register_2_q), .clk(CLK));  // open: clr
  Register #(.width(4)) register_3 (.D(Write_Data), .en(and_3_out), .Q(register_3_q), .clk(CLK));  // open: clr
  Register #(.width(4)) register_4 (.D(Write_Data), .en(and_4_out), .Q(register_4_q), .clk(CLK));  // open: clr
  Register #(.width(4)) register_5 (.D(Write_Data), .en(and_5_out), .Q(register_5_q), .clk(CLK));  // open: clr
  Register #(.width(4)) register_6 (.D(Write_Data), .en(and_6_out), .Q(register_6_q), .clk(CLK));  // open: clr
  Register #(.width(4)) register_7 (.D(Write_Data), .en(and_7_out), .Q(register_7_q), .clk(CLK));  // open: clr
  Register #(.width(4)) register_8 (.D(Write_Data), .en(and_8_out), .Q(register_8_q), .clk(CLK));  // open: clr
  Multiplexer #(.select(3), .width(4)) multiplexer_1 (
    .in0(register_1_q), .in1(register_2_q), .in2(register_3_q), .in3(register_4_q), .in4(register_5_q),
    .in5(register_6_q), .in6(register_7_q), .in7(register_8_q), .out(Read_Data_1), .sel(RS));  // open: en
  Multiplexer #(.select(3), .width(4)) multiplexer_2 (
    .in0(register_1_q), .in1(register_2_q), .in2(register_3_q), .in3(register_4_q), .in4(register_5_q),
    .in5(register_6_q), .in6(register_7_q), .in7(register_8_q), .out(Read_Data_2), .sel(RD));  // open: en
endmodule
