// Logisim project  lab6_classwork_cse332l.5_fall2020.circ as structural Verilog: 4 circuits, main circuit main
module main (
  input  [2:0] Read_Register_1,
  input  Cin,
  input  [2:0] Read_Register_2,
  input  [2:0] Write_Register,
  input  Write_Control,
  input  CLK,
  input  [1:0] Select_Operation,
  output Cout
);

  wire [3:0] n4_bit_alu_1_output, n4_bit_register_1_read_data_1, n4_bit_register_1_read_data_2;

  _4_bit_Register u_4_bit_register_1 (
    .Write_Data(n4_bit_alu_1_output), .Write_Control(Write_Control), .CLK(CLK),
    .Read_Data_1(n4_bit_register_1_read_data_1), .Write_register(Write_Register), .RS(Read_Register_1),
    .Read_Data_2(n4_bit_register_1_read_data_2), .RD(Read_Register_2));
  _4_bit_ALU u_4_bit_alu_1 (
    .Cin(Cin), .A3__A2__A1__A0(n4_bit_register_1_read_data_1),
    .B3__B2__B1__B0(n4_bit_register_1_read_data_2), .Select_Operation(Select_Operation),
    .Output(n4_bit_alu_1_output), .Cout(Cout));
endmodule

module _1_bit_ALU (
  input  Cin,
  input  A,
  input  B,
  input  [2:0] Operation_Selection,
  output Output,
  output Cout
);

  wire adder_1_out, and_1_out, not_1_out, not_2_out, xor_1_out;

  not not_1 (not_1_out, B);
  not not_2 (not_2_out, A);
  and and_1 (and_1_out, A, B);
  xor xor_1 (xor_1_out, A, B);
  Adder #(.width(1)) adder_1 (.a(A), .b(B), .out(adder_1_out), .cin(Cin), .cout(Cout));
  Multiplexer #(.select(3)) multiplexer_1 (
    .in2(and_1_out), .in3(xor_1_out), .in4(adder_1_out), .in5(not_2_out), .in6(not_1_out), .out(Output),
    .sel(Operation_Selection));  // open: in0, in1, in7, en
endmodule

module _4_bit_ALU (
  input  Cin,
  input  [3:0] A3__A2__A1__A0,
  input  [3:0] B3__B2__B1__B0,
  input  [1:0] Select_Operation,
  output [3:0] Output,
  output Cout
);

  wire n1_bit_alu_1_cout, n1_bit_alu_2_cout, n1_bit_alu_3_cout;
  wire [2:2] undriven;

  _1_bit_ALU u_1_bit_alu_1 (
    .Cin(Cin), .A(A3__A2__A1__A0[0]), .B(B3__B2__B1__B0[0]), .Output(Output[0]), .Cout(n1_bit_alu_1_cout),
    .Operation_Selection({undriven[2], Select_Operation}));
  _1_bit_ALU u_1_bit_alu_2 (
    .Cin(n1_bit_alu_1_cout), .A(A3__A2__A1__A0[1]), .B(B3__B2__B1__B0[1]), .Output(Output[1]),
    .Cout(n1_bit_alu_2_cout), .Operation_Selection({undriven[2], Select_Operation}));
  _1_bit_ALU u_1_bit_alu_3 (
    .Cin(n1_bit_alu_2_cout), .A(A3__A2__A1__A0[2]), .B(B3__B2__B1__B0[2]), .Output(Output[2]),
    .Cout(n1_bit_alu_3_cout), .Operation_Selection({undriven[2], Select_Operation}));
  _1_bit_ALU u_1_bit_alu_4 (
    .Cin(n1_bit_alu_3_cout), .A(A3__A2__A1__A0[3]), .B(B3__B2__B1__B0[3]), .Output(Output[3]), .Cout(Cout),
    .Operation_Selection({undriven[2], Select_Operation}));
  // Pins of 2 and 3 bits meet at {undriven[2], Select_Operation}
endmodule

module _4_bit_Register (
  input  [2:0] Write_register,
  input  [2:0] RS,
  input  [2:0] RD,
  input  [3:0] Write_Data,
  input  Write_Control,
  input  CLK,
  output [3:0] Read_Data_1,
  output [3:0] Read_Data_2
);

  wire and_1_out, and_2_out, and_3_out, and_4_out, and_5_out, and_6_out, and_7_out, and_8_out,
       decoder_1_out0, decoder_1_out1, decoder_1_out2, decoder_1_out3, decoder_1_out4, decoder_1_out5,
       decoder_1_out6, decoder_1_out7;
  wire [3:0] register_1_q, register_2_q, register_3_q, register_4_q, register_5_q, register_6_q,
       register_7_q, register_8_q;

  Decoder #(.select(3)) decoder_1 (
    .out0(decoder_1_out0), .out1(decoder_1_out1), .out2(decoder_1_out2), .out3(decoder_1_out3),
    .out4(decoder_1_out4), .out5(decoder_1_out5), .out6(decoder_1_out6), .out7(decoder_1_out7),
    .sel(Write_register));  // open: en
  and and_1 (and_1_out, decoder_1_out0, Write_Control);
  and and_2 (and_2_out, decoder_1_out1, Write_Control);
  and and_3 (and_3_out, decoder_1_out2, Write_Control);
  and and_4 (and_4_out, decoder_1_out3, Write_Control);
  and and_5 (and_5_out, decoder_1_out4, Write_Control);
  and and_6 (and_6_out, decoder_1_out5, Write_Control);
  and and_7 (and_7_out, decoder_1_out6, Write_Control);
  and and_8 (and_8_out, decoder_1_out7, Write_Control);
  Register #(.width(4)) register_1 (.D(Write_Data), .en(and_1_out), .Q(register_1_q), .clk(CLK));  // open: clr
  Register #(.width(4)) register_2 (.D(Write_Data), .en(and_2_out), .Q(register_2_q), .clk(CLK));  // open: clr
  Register #(.width(4)) register_3 (.D(Write_Data), .en(and_3_out), .Q(register_3_q), .clk(CLK));  // open: clr
  Register #(.width(4)) register_4 (.D(Write_Data), .en(and_4_out), .Q(register_4_q), .clk(CLK));  // open: clr
  Register #(.width(4)) register_5 (.D(Write_Data), .en(and_5_out), .Q(register_5_q), .clk(CLK));  // open: clr
  Register #(.width(4)) register_6 (.D(Write_Data), .en(and_6_out), .Q(register_6_q), .clk(CLK));  // open: clr
  Register #(.width(4)) register_7 (.D(Write_Data), .en(and_7_out), .Q(register_7_q), .clk(CLK));  // open: clr
  Register #(.width(4)) register_8 (.D(Write_Data), .en(and_8_out), .Q(register_8_q), .clk(CLK));  // open: clr
  Multiplexer #(.select(3), .width(4)) multiplexer_1 (
    .in0(register_1_q), .in1(register_2_q), .in2(register_3_q), .in3(register_4_q), .in4(register_5_q),
    .in5(register_6_q), .in6(register_7_q), .in7(register_8_q), .out(Read_Data_1), .sel(RS));  // open: en
  Multiplexer #(.select(3), .width(4)) multiplexer_2 (
    .in0(register_1_q), .in1(register_2_q), .in2(register_3_q), .in3(register_4_q), .in4(register_5_q),
    .in5(register_6_q), .in6(register_7_q), .in7(register_8_q), .out(Read_Data_2), .sel(RD));  // open: en
endmodule
