// Logisim project CSE332l_05_LAB_02_CLASSWORK.circ as structural Verilog: 1 circuit, main circuit main
module main (
  input  Cin,
  input  [1:0] S1__S0,
  input  B0,
  input  A0,
  input  in_5,
  input  in_6,
  input  B1,
  input  A1,
  input  in_9,
  input  in_10,
  output D0,
  output D1,
  output Cout
);

  wire adder_1_cout, multiplexer_1_out, multiplexer_2_out, not_1_out, not_2_out;

  not not_1 (not_1_out, B0);
  not not_2 (not_2_out, B1);
  Multiplexer #(.select(2)) multiplexer_1 (
    .in0(B0), .in1(not_1_out), .in2(in_5), .in3(in_6), .out(multiplexer_1_out), .sel(S1__S0));  // open: en
  Multiplexer #(.select(2)) multiplexer_2 (
    .in0(B1), .in1(not_2_out), .in2(in_9), .in3(in_10), .out(multiplexer_2_out), .sel(S1__S0));  // open: en
  Adder #(.width(1)) adder_1 (.a(A0), .b(multiplexer_1_out), .out(D0), .cin(Cin), .cout(adder_1_cout));
  Adder #(.width(1)) adder_2 (.a(A1), .b(multiplexer_2_out), .out(D1), .cin(adder_1_cout), .cout(Cout));
endmodule
